# Fritzing sketch ArdunioI2C (saved by Fritzing 0.9.3b)
breadboards: 1

parts:
  元件3 = Arduino Pro Mini v13
  元件4 = Arduino Leonardo (Rev3b)
  R1 = Resistor [tolerance=±5% resistance=4.7k package=THT]
  R2 = Resistor [tolerance=±5% resistance=4.7k package=THT]

nets:
  VCC: 元件3.VCC, 元件4.5V, R1.Pin_0, R2.Pin_0
  N1: 元件3.D5_PWM, 元件4.A5, R2.Pin_1
  N2: 元件3.D4, 元件4.A4, R1.Pin_1
